# Fritzing sketch Cau11-quangtro-1led (saved by Fritzing 0.9.3b)
breadboards: 1

parts:
  R1 = Photocell (LDR) [package=THT]
  R2 = Resistor [tolerance=±5% resistance=220 package=THT]
  LED1 = LED - 5mm [color="Red (633nm)" package="5 mm [THT]"]
  R3 = Resistor [tolerance=±5% resistance=220 package=THT]
  Part1 = Arduino Uno (Rev3) - ICSP

nets:
  N1: R1.pin_0, Part1.5V
  N2: R1.pin_1, R2.Pin_0, Part1.A1
  N3: R2.Pin_1, LED1.cathode, Part1.GND
  N4: LED1.anode, R3.Pin_0
  N5: R3.Pin_1, Part1.D9_PWM

// code stored in the sketch: Cau10-quangtro-1led.ino
const int LDR_PIN = A1;
const int LED_PIN = 9;
int lightValue = 0;

void setup() {
  pinMode(LED_PIN, OUTPUT);
  Serial.begin(9600);
}

void loop() {
  lightValue = analogRead(LDR_PIN);
  Serial.print("Giá tr? ánh sáng: ");
  Serial.print(lightValue);

  if (lightValue > 500) {
    digitalWrite(LED_PIN, LOW); // T?t ?èn
    Serial.println(" -> ?èn LED t?t");
  } else {
    digitalWrite(LED_PIN, HIGH); // B?t ?èn
    Serial.println(" -> ?èn LED sáng");
  }

  delay(500);
}
