# Fritzing sketch Cau12-quangtro-RGB (saved by Fritzing 0.9.3b)
breadboards: 1

parts:
  Part2 = Arduino Uno (Rev3) - ICSP
  R4 = Photocell (LDR) [package=THT]
  R5 = Resistor [tolerance=±5% resistance=220 package=THT]
  R6 = Resistor [tolerance=±5% resistance=220 package=THT]
  LED1 = RGB LED (com. cathode, rgb) [package="5 mm [THT]"]
  R7 = Resistor [tolerance=±5% resistance=220 package=THT]
  R8 = Resistor [tolerance=±5% resistance=220 package=THT]

nets:
  N1: Part2.A1, R4.pin_1, R5.Pin_0
  N2: Part2.D9_PWM, R6.Pin_0
  N3: Part2.D10_PWM/SS, R8.Pin_0
  N4: Part2.D11_PWM/MOSI, R7.Pin_0
  N5: Part2.5V, R4.pin_0
  N6: Part2.GND, R5.Pin_1, LED1.common_cathode
  N7: R6.Pin_1, LED1.red_anode
  N8: LED1.green_anode, R7.Pin_1
  N9: LED1.blue_anode, R8.Pin_1

// code stored in the sketch: Cau12-quangtro-RGB.ino
const int LDR_PIN = A1;
const int RED_PIN = 9;
const int GREEN_PIN = 10;
const int BLUE_PIN = 11;
int lightValue = 0;

void setup() {
  pinMode(RED_PIN, OUTPUT);
  pinMode(GREEN_PIN, OUTPUT);
  pinMode(BLUE_PIN, OUTPUT);
  Serial.begin(9600);
}

void loop() {
  lightValue = analogRead(LDR_PIN);
  Serial.print("Giá tr? ánh sáng: ");
  Serial.print(lightValue);

  if (lightValue <= 200) {
    setColor(255, 0, 0); // ??
    Serial.println(" -> ?èn RGB sáng màu: ??");
  } else if (lightValue <= 400) {
    setColor(0, 255, 0); // xanh lá
    Serial.println(" -> ?èn RGB sáng màu: xanh lá");
  } else if (lightValue <= 500) {
    setColor(0, 0, 255); // xanh d??ng
    Serial.println(" -> ?èn RGB sáng màu: xanh d??ng");
  } else {
    setColor(255, 255, 255); // tr?ng (sáng c? 3 màu)
    Serial.println(" -> ?èn RGB sáng màu: tr?ng");
  }

  delay(500);
}

void setColor(int redVal, int greenVal, int blueVal) {
  analogWrite(RED_PIN, redVal);
  analogWrite(GREEN_PIN, greenVal);
  analogWrite(BLUE_PIN, blueVal);
}
