# Fritzing sketch Cau15-LCD-quangtro-nhietdo (saved by Fritzing 0.9.3b)
breadboards: 1

parts:
  Part2 = Arduino Uno (Rev3) - ICSP
  U5 = LCD-16X2 [package=lcd-16x2]
  U6 = POT_SWITCH [package=pot_pth_switch]
  R4 = Resistor [tolerance=±5% resistance=220 package=THT]
  R5 = Photocell (LDR) [package=THT]
  R6 = Resistor [tolerance=±5% resistance=220 package=THT]

nets:
  N1: Part2.A0, R5.pin_1, R6.Pin_0
  N2: Part2.ICSP_MISO, Part2.D12/MISO, U5.RS
  N3: Part2.D11_PWM/MOSI, U5.E
  N4: Part2.D4, U5.DB4
  N5: Part2.D5_PWM, U5.DB5
  N6: Part2.D6_PWM, U5.DB6
  N7: Part2.D7, U5.DB7
  5V: Part2.5V, U5.VDD, U5.K, U6.G$1_A, R4.Pin_1, R5.pin_0
  GND: Part2.GND, U5.VSS, U5.R_W, U6.G$2_2, R6.Pin_1
  N8: U5.VO, U6.G$2_1
  N9: U5.A, R4.Pin_0

// code stored in the sketch: Cau15-LCD-quangtro-nhietdo.ino
#include <LiquidCrystal.h>

// RS = 12, E = 11, D4 = 4, D5 = 5, D6 = 6, D7 = 7
LiquidCrystal lcd(12, 11, 4, 5, 6, 7);

const int P2_PIN = A0;
int analogValue = 0;
int nhietDo = 0;

void setup() {
  lcd.begin(16, 2);
}

void loop() {
  analogValue = analogRead(P2_PIN);
  nhietDo = map(analogValue, 0, 1023, 0, 100);

  lcd.clear();
  lcd.setCursor(0, 0);
  lcd.print("Gia tri ADC: ");
  lcd.print(analogValue);

  lcd.setCursor(0, 1);
  lcd.print("Nhiet do: ");
  lcd.print(nhietDo);
  lcd.print(" C");

  delay(1000);
}
