# Fritzing sketch Cau16-LCD-quangtro-nhietdo-in-cuon (saved by Fritzing 0.9.3b)
breadboards: 1

parts:
  Part3 = Arduino Uno (Rev3) - ICSP
  U7 = LCD-16X2 [package=lcd-16x2]
  U8 = POT_SWITCH [package=pot_pth_switch]
  R7 = Resistor [tolerance=±5% resistance=220 package=THT]
  R8 = Photocell (LDR) [package=THT]
  R9 = Resistor [tolerance=±5% resistance=220 package=THT]

nets:
  N1: Part3.A0, R8.pin_1, R9.Pin_0
  N2: Part3.ICSP_MISO, Part3.D12/MISO, U7.RS
  N3: Part3.D11_PWM/MOSI, U7.E
  N4: Part3.D4, U7.DB4
  N5: Part3.D5_PWM, U7.DB5
  N6: Part3.D6_PWM, U7.DB6
  N7: Part3.D7, U7.DB7
  5V: Part3.5V, U7.VDD, U7.K, U8.G$1_A, R7.Pin_1, R8.pin_0
  GND: Part3.GND, U7.VSS, U7.R_W, U8.G$2_2, R9.Pin_1
  N8: U7.VO, U8.G$2_1
  N9: U7.A, R7.Pin_0

// code stored in the sketch: Cau16-LCD-quangtro-nhietdo-in-cuon.ino
#include <LiquidCrystal.h>

// RS = 12, E = 11, D4 = 4, D5 = 5, D6 = 6, D7 = 7
LiquidCrystal lcd(12, 11, 4, 5, 6, 7);

const int LDR_PIN = A0;
int analogValue = 0;
int nhietDo = 0;

void setup() {
  lcd.begin(16, 2);
}

void loop() {
  analogValue = analogRead(LDR_PIN);
  nhietDo = map(analogValue, 0, 1023, 0, 100);

  // Nh?p nháy 3 l?n
  for (int i = 0; i < 3; i++) {
    lcd.clear();
    lcd.setCursor(0, 0);
    lcd.print("CHAO NGAY MOI");
    lcd.setCursor(0, 1);
    lcd.print("Nhiet do: ");
    lcd.print(nhietDo);
    lcd.print(" C");
    delay(500);
    lcd.clear();
    delay(500);
  }

  // Hi?n th? l?i và di chuy?n t? trái qua ph?i
  lcd.setCursor(0, 0);
  lcd.print("CHAO NGAY MOI");
  lcd.setCursor(0, 1);
  lcd.print("Nhiet do: ");
  lcd.print(nhietDo);
  lcd.print(" C");

  for (int i = 0; i < 16; i++) {
    lcd.scrollDisplayRight();
    delay(300);
  }

  delay(1000);
}
