# Fritzing sketch Cau17-LCD-Nhap_cuonlai (saved by Fritzing 0.9.3b)
breadboards: 1

parts:
  Part4 = Arduino Uno (Rev3) - ICSP
  U7 = LCD-16X2 [package=lcd-16x2]
  U8 = POT_SWITCH [package=pot_pth_switch]
  R4 = Resistor [tolerance=±5% resistance=220 package=THT]

nets:
  N1: Part4.ICSP_MISO, Part4.D12/MISO, U7.RS
  N2: Part4.D11_PWM/MOSI, U7.E
  N3: Part4.D4, U7.DB4
  N4: Part4.D5_PWM, U7.DB5
  N5: Part4.D6_PWM, U7.DB6
  N6: Part4.D7, U7.DB7
  5V: Part4.5V, U7.VDD, U7.K, U8.G$1_A, R4.Pin_1
  GND: Part4.GND, U7.VSS, U7.R_W, U8.G$2_2
  N7: U7.VO, U8.G$2_1
  N8: U7.A, R4.Pin_0

// code stored in the sketch: Cau17-LCD-Nhap_cuonlai.ino
#include <LiquidCrystal.h>

LiquidCrystal lcd(12, 11, 4, 5, 6, 7);
String text; 

void setup() {
  Serial.begin(9600);
  lcd.begin(16, 2);
  lcd.print("Nhap chuoi:");
}

void loop() {
  // 1) ??c chu?i t? Serial
  if (Serial.available()) {
    text = Serial.readStringUntil('\n');
    text.trim();
    
    // 2) Hi?n th? chu?i lên LCD
    lcd.clear();
    lcd.setCursor(0, 0);
    lcd.print(text);
    
    // 3) ??i 2s
    delay(2000);
    
    // 4) Nh?p nháy 3 l?n
    for (int i = 0; i < 3; i++) {
      lcd.clear();
      delay(300);
      lcd.setCursor(0, 0);
      lcd.print(text);
      delay(300);
    }
    
    // 5) Cu?n ch? t? ph?i sang trái
    //    In l?i ? v? trí ban ??u
    lcd.clear();
    lcd.setCursor(16 - min((int)text.length(), 16), 0);
    lcd.print(text);
    //    Cu?n
    int scrollCount = (int)text.length() + 16;
    for (int i = 0; i < scrollCount; i++) {
      lcd.scrollDisplayLeft();
      delay(300);
    }
    
    // Quay l?i yêu c?u nh?p m?i
    lcd.clear();
    lcd.print("Nhap chuoi:");
  }
}
