# Fritzing sketch Cau2-2uno-1nut-1coi (saved by Fritzing 0.9.3b)
breadboards: 1

parts:
  Part3 = Arduino Uno (Rev3) - ICSP
  Part4 = Arduino Uno (Rev3) - ICSP
  J2 = Piezo Speaker
  S1 = Pushbutton [package="[THT]"]
  R1 = Resistor [tolerance=±5% resistance=220 package=THT]

nets:
  N1: Part3.D1/TX, Part4.D0/RX
  N2: Part3.D7, S1.Pin_1, S1.Pin_2, R1.Pin_0
  N3: Part3.5V, R1.Pin_1
  GND: Part3.GND, Part4.GND, J2.pin1, S1.Pin_3, S1.Pin_4

// code stored in the sketch: Cau2-2uno-1nut-1coi.ino
//  Arduino 1
const int buttonPin = 7;

void setup() {
  pinMode(buttonPin, INPUT);
  Serial.begin(9600);
}

void loop() {
  int buttonState = digitalRead(buttonPin);
  Serial.println(buttonState); // G?i tr?ng thái nút nh?n
  delay(100);
}

//  Arduino 1
const int buzzerPin = 3;

void setup() {
  pinMode(buzzerPin, OUTPUT);
  Serial.begin(9600);
}

void loop() {
  if (Serial.available()) {
    int buttonState = Serial.parseInt();
    if (buttonState == LOW) {
      tone(buzzerPin, 10000);
    } else {
      noTone(buzzerPin);
    }
  }
}
