# Fritzing sketch Cau3-2uno-1nut-1servo (saved by Fritzing 0.9.3b)
breadboards: 1

parts:
  Part5 = Arduino Uno (Rev3) - ICSP
  Part6 = Arduino Uno (Rev3) - ICSP
  S2 = Pushbutton [package="[THT]"]
  R2 = Resistor [tolerance=±5% resistance=220 package=THT]
  J1 = Basic Servo

nets:
  N1: Part5.D9_PWM, J1.pulse
  N2: Part5.D0/RX, Part6.D1/TX
  5V: Part5.5V, J1.vcc
  GND: Part5.GND, Part6.GND, S2.Pin_3, S2.Pin_4, J1.gnd
  N3: Part6.D7, S2.Pin_1, S2.Pin_2, R2.Pin_0
  N4: Part6.5V, R2.Pin_1

// code stored in the sketch: Cau3-2uno-1nut-1servo.ino
const int buttonPin = 7;

void setup() {
  pinMode(buttonPin, INPUT);
  Serial.begin(9600);
}

void loop() {
  int buttonState = digitalRead(buttonPin);
  Serial.println(buttonState); // G?i tr?ng thái nút nh?n
  delay(100);
}

// Arduino 2

#include <Servo.h>

Servo myServo;
const int servoPin = 9;

void setup() {
  myServo.attach(servoPin);
  Serial.begin(9600);
}

void loop() {
  if (Serial.available()) {
    int buttonState = Serial.parseInt();
    if (buttonState == LOW) {
      myServo.write(60); // Quay ??n góc 60°
    } else {
      myServo.write(0); // Quay v? góc 0°
    }
  }
}
