# Fritzing sketch Cau38-coi-servo (saved by Fritzing 0.9.3b)
breadboards: 1

parts:
  J1 = Piezo Speaker
  J2 = Basic Servo
  Part1 = Arduino Uno (Rev3) - ICSP

nets:
  GND: J1.pin1, J2.gnd, Part1.GND
  N1: J1.pin2, Part1.D6_PWM
  VCC: J2.vcc, Part1.5V
  N2: J2.pulse, Part1.D5_PWM

// code stored in the sketch: Cau38-coi-servo.ino
#include <Servo.h>

Servo myServo;
int buzzerPin = 6;

void setup() {
  myServo.attach(5);       // G?n servo vào chân 5
  pinMode(buzzerPin, OUTPUT);
  randomSeed(analogRead(0)); // T?o seed cho s? ng?u nhiên
}

void loop() {
  int a = random(0, 181);   // T?o s? ng?u nhiên t? 0 ??n 180
  myServo.write(a);         // ?i?u khi?n servo quay ??n góc a
  tone(buzzerPin, a * 100); // Phát âm thanh v?i t?n s? a * 100 Hz
  delay(500);               // Kêu trong 0.5s
  noTone(buzzerPin);        // T?t buzzer
  delay(4500);              // Ch? ??n h?t chu k? 5s
}
