# Fritzing sketch Cau4-2uno-1quangtro-1servo (saved by Fritzing 0.9.3b)
breadboards: 1

parts:
  Part7 = Arduino Uno (Rev3) - ICSP
  Part8 = Arduino Uno (Rev3) - ICSP
  R3 = Resistor [tolerance=±5% resistance=220 package=THT]
  J2 = Basic Servo
  R4 = Photocell (LDR) [package=THT]

nets:
  N1: Part7.D12/MISO, J2.pulse
  N2: Part7.D0/RX, Part8.D1/TX
  5V: Part7.5V, J2.vcc
  GND: Part7.GND, Part8.GND, R3.Pin_1, J2.gnd
  N3: Part8.A3, R3.Pin_0, R4.pin_1
  N4: Part8.5V, R4.pin_0

// code stored in the sketch: Cau4-2uno-1quangtro-1servo.ino
// Thi?t b? A
void setup() {
  Serial.begin(9600);
}

void loop() {
  int sensorValue = analogRead(A3); // ??c giá tr? t? quang tr?
  int angle = constrain(sensorValue / 6, 0, 180); // Chuy?n v? góc 0-180
  Serial.println(angle); // G?i d? li?u qua Serial
  delay(100);
}

#include <Servo.h>

Servo myServo;

void setup() {
  Serial.begin(9600);
  myServo.attach(12); // G?n Servo vào chân 12
}

void loop() {
  if (Serial.available()) {
    int angle = Serial.parseInt(); // Nh?n d? li?u t? A
    myServo.write(angle); // ?i?u khi?n Servo
  }
}
