# Fritzing sketch Cau42-coi-4-nut (saved by Fritzing 0.9.3b)
breadboards: 1

parts:
  J1 = Piezo Speaker
  Part1 = Arduino Uno (Rev3) - ICSP
  S1 = Pushbutton [package="[THT]"]
  R1 = Resistor [tolerance=±5% resistance=220 package=THT]
  S2 = Pushbutton [package="[THT]"]
  R2 = Resistor [tolerance=±5% resistance=220 package=THT]
  S3 = Pushbutton [package="[THT]"]
  R3 = Resistor [tolerance=±5% resistance=220 package=THT]
  S4 = Pushbutton [package="[THT]"]
  R4 = Resistor [tolerance=±5% resistance=220 package=THT]

nets:
  N1: J1.pin1, R1.Pin_1, R2.Pin_1, R3.Pin_1, R4.Pin_1
  N2: J1.pin2, Part1.D7
  N3: Part1.D3_PWM, S1.Pin_1, S1.Pin_2, R1.Pin_0
  N4: Part1.D4, S2.Pin_1, S2.Pin_2, R2.Pin_0
  N5: Part1.D5_PWM, S3.Pin_1, S3.Pin_2, R3.Pin_0
  N6: Part1.D6_PWM, S4.Pin_1, S4.Pin_2, R4.Pin_0
  N7: S1.Pin_3, S1.Pin_4, S2.Pin_3, S2.Pin_4, S3.Pin_3, S3.Pin_4, S4.Pin_3, S4.Pin_4

// code stored in the sketch: Cau42-coi-4-nut.ino
int buttons[] = {3, 4, 5, 6};
int tones[] = {10, 500, 1000, 6000};
int buzzer = 7;

void setup() {
  for (int i = 0; i < 4; i++) {
    pinMode(buttons[i], INPUT);
  }
  pinMode(buzzer, OUTPUT);
}

void loop() {
  for (int i = 0; i < 4; i++) {
    if (digitalRead(buttons[i]) == HIGH) {
      delay(50); // Ch?ng d?i
      tone(buzzer, tones[i]); // Phát âm thanh
      delay(1000);
      noTone(buzzer); // T?t còi

      // ??i ng??i dùng nh? nút
      while (digitalRead(buttons[i]) == HIGH) {
        delay(10);
      }
    }
  }
}
