# Fritzing sketch Cau43-servo-bientro (saved by Fritzing 0.9.3b)
breadboards: 1

parts:
  Part1 = Arduino Uno (Rev3) - ICSP
  U1 = POT_SWITCH [package=pot_pth_switch]
  J1 = Basic Servo

nets:
  N1: Part1.A0, U1.G$2_1
  5V: Part1.5V, U1.G$1_A, J1.vcc
  GND: Part1.GND, U1.G$2_2, J1.gnd

// code stored in the sketch: cau43-servo-poten.ino
#include <Servo.h>

Servo myServo;
int bienTro = A0;

void setup() {
  myServo.attach(5);
}

void loop() {
  int a = analogRead(bienTro);
  int goc = map(a, 0, 1023, 0, 180);
  myServo.write(goc);
  delay(15); // ??i servo quay
}
