# Fritzing sketch Cau44-4-nut-servo (saved by Fritzing 0.9.3b)
breadboards: 1

parts:
  Part1 = Arduino Uno (Rev3) - ICSP
  J1 = Basic Servo
  S1 = Pushbutton [package="[THT]"]
  R1 = Resistor [tolerance=±5% resistance=220 package=THT]
  S2 = Pushbutton [package="[THT]"]
  R2 = Resistor [tolerance=±5% resistance=220 package=THT]
  S3 = Pushbutton [package="[THT]"]
  R3 = Resistor [tolerance=±5% resistance=220 package=THT]
  S4 = Pushbutton [package="[THT]"]
  R4 = Resistor [tolerance=±5% resistance=220 package=THT]

nets:
  N1: Part1.D3_PWM, S1.Pin_1, S1.Pin_2, R1.Pin_0
  N2: Part1.D4, S2.Pin_1, S2.Pin_2, R2.Pin_0
  N3: Part1.D5_PWM, S3.Pin_1, S3.Pin_2, R3.Pin_0
  N4: Part1.D6_PWM, S4.Pin_1, S4.Pin_2, R4.Pin_0
  N5: Part1.D7, J1.pulse
  5V: Part1.5V, J1.vcc, S1.Pin_3, S1.Pin_4, S2.Pin_3, S2.Pin_4, S3.Pin_3, S3.Pin_4, S4.Pin_3, S4.Pin_4
  GND: Part1.GND, J1.gnd, R1.Pin_1, R2.Pin_1, R3.Pin_1, R4.Pin_1

// code stored in the sketch: cau44-4-nut-servo.ino
#include <Servo.h>

Servo myServo;
int buttons[] = {3, 4, 5, 6};
int angles[] = {45, 90, 135, 180};
int buttonState[4];

void setup() {
  myServo.attach(7);
  myServo.write(0); 

  for (int i = 0; i < 4; i++) {
    pinMode(buttons[i], INPUT);
  }
}

void loop() {
  for (int i = 0; i < 4; i++) {
    if (digitalRead(buttons[i]) == HIGH) {
      myServo.write(angles[i]);
      delay(3000);
      myServo.write(0);
    }
  }
}
