# Fritzing sketch Cau5-2uno-1bientro-1coi (saved by Fritzing 0.9.3b)
breadboards: 1

parts:
  Part3 = Arduino Uno (Rev3) - ICSP
  Part4 = Arduino Uno (Rev3) - ICSP
  U2 = POT_SWITCH [package=pot_pth_switch]
  J2 = Piezo Speaker

nets:
  N1: Part3.A1, U2.G$2_1
  N2: Part3.D1/TX, Part4.D0/RX
  N3: Part3.5V, U2.G$2_2
  GND: Part3.GND, Part4.GND, U2.G$1_A, J2.pin1
  N4: Part4.D3_PWM, J2.pin2

// code stored in the sketch: Cau5-2uno-1bientro-1coi.ino
void setup() {
  Serial.begin(9600);
}

void loop() {
  int b = analogRead(A4) / 10; // Gi?m ?? phân gi?i
  int a = (b + 1) * 10;
  Serial.println(a); // G?i t?n s? a
  delay(100);
}
//2
#define BUZZER_PIN 8

void setup() {
  Serial.begin(9600);
  pinMode(BUZZER_PIN, OUTPUT);
}

void loop() {
  if (Serial.available()) {
    int freq = Serial.parseInt(); // Nh?n t?n s?
    tone(BUZZER_PIN, freq);       // Phát âm v?i t?n s? a
    delay(100);
    noTone(BUZZER_PIN);           // T?t t?m th?i ?? nghe rõ ti?ng
  }
}
