# Fritzing sketch Cau6-2uno-1nut-1net (saved by Fritzing 0.9.3b)
breadboards: 1

parts:
  Part5 = Arduino Uno (Rev3) - ICSP
  Part6 = Arduino Uno (Rev3) - ICSP
  S2 = Pushbutton [package="[THT]"]
  R2 = Resistor [tolerance=±5% resistance=220 package=THT]
  LED1 = LED - 5mm [color="Red (633nm)" package="5 mm [THT]"]
  R3 = Resistor [tolerance=±5% resistance=220 package=THT]

nets:
  N1: Part5.D0/RX, Part6.D1/TX
  N2: Part5.D6_PWM, R3.Pin_1
  GND: Part5.GND, Part6.GND, S2.Pin_3, S2.Pin_4, LED1.cathode
  N3: Part6.D7, S2.Pin_1, S2.Pin_2, R2.Pin_0
  N4: Part6.5V, R2.Pin_1
  N5: LED1.anode, R3.Pin_0

// code stored in the sketch: Cau6-2uno-1nut-1net.ino
#define BUTTON_PIN 7

void setup() {
  pinMode(BUTTON_PIN, INPUT);
  Serial.begin(9600);
}

void loop() {
  int buttonState = digitalRead(BUTTON_PIN);
  Serial.println(buttonState); // 1 n?u b?m, 0 n?u không
  delay(100);
}



#define LED_PIN 6

unsigned long lastToggle = 0;
int ledState = LOW;
int interval = 2000;

void setup() {
  pinMode(LED_PIN, OUTPUT);
  Serial.begin(9600);
}

void loop() {
  if (Serial.available()) {
    int state = Serial.parseInt();
    interval = (state == HIGH) ? 1000 : 2000; // ??i t?c ?? nh?p nháy
  }

  if (millis() - lastToggle >= interval) {
    lastToggle = millis();
    ledState = !ledState;
    digitalWrite(LED_PIN, ledState);
  }
}
