# Fritzing sketch cau1-2uno-1bientro-1coi (saved by Fritzing 0.9.3b)
breadboards: 1

parts:
  Part1 = Arduino Uno (Rev3) - ICSP
  Part2 = Arduino Uno (Rev3) - ICSP
  U1 = POT_SWITCH [package=pot_pth_switch]
  J1 = Piezo Speaker

nets:
  N1: Part1.A1, U1.G$2_1
  N2: Part1.D1/TX, Part2.D0/RX
  N3: Part1.5V, U1.G$2_2
  GND: Part1.GND, Part2.GND, U1.G$1_A, J1.pin1
  N4: Part2.D3_PWM, J1.pin2

// code stored in the sketch: cau1-2uno-1bientro-1coi.ino
//  Arduino 1
void setup() {
  Serial.begin(9600);
}

void loop() {
  int a = analogRead(A1);
  Serial.println(a); // G?i giá tr? bi?n tr?
  delay(100);
}

// Arduino 2
const int buzzerPin = 3;

void setup() {
  Serial.begin(9600);
  pinMode(buzzerPin, OUTPUT);
}

void loop() {
  if (Serial.available()) {
    int a = Serial.parseInt(); // ??c giá tr? t? thi?t b? A
    if (a < 512) {
      tone(buzzerPin, 10000); // Kêu v?i t?n s? 10000Hz
    } else {
      noTone(buzzerPin); // Ng?ng kêu
    }
  }
}
