# Fritzing sketch cau10_Coi_NutNhan (saved by Fritzing 0.9.3b)
breadboards: 1

parts:
  Part2 = Arduino Uno (Rev3) - ICSP
  J2 = Piezo Speaker
  S1 = Pushbutton [package="[THT]"]
  R1 = Resistor [tolerance=±5% resistance=220 package=THT]

nets:
  N1: Part2.D8, J2.pin2
  N2: Part2.D2, S1.Pin_1, S1.Pin_2, R1.Pin_0
  N3: Part2.5V, S1.Pin_3, S1.Pin_4
  N4: Part2.GND, J2.pin1, R1.Pin_1

// code stored in the sketch: Bai10_Coi_NutNhan.ino
const int buttonPin = 2;    // Nút nh?n n?i chân D2
const int buzzerPin = 8;    // Còi n?i chân D8

void setup() {
  Serial.begin(9600);
  pinMode(buttonPin, INPUT); // Kích ho?t ?i?n tr? kéo lên n?i b?
  pinMode(buzzerPin, OUTPUT);
}

void loop() {
  int buttonState = digitalRead(buttonPin);

  if (buttonState == HIGH) {  // Nút nh?n ???c nh?n (vì pullup nên LOW)
    digitalWrite(buzzerPin, HIGH);
    Serial.println("Nut nhan dang duoc nhan, coi dang keu");
  } 
  else {                     // Nút th? ra
    digitalWrite(buzzerPin, LOW);
    Serial.println("Nut nhan khong duoc nhan, coi ngung keu");
  }

  delay(200);
}
