# Fritzing sketch cau13-quangtro-1led-sangdan (saved by Fritzing 0.9.3b)
breadboards: 1

parts:
  R5 = Resistor [tolerance=±5% resistance=220 package=THT]
  R6 = Resistor [tolerance=±5% resistance=220 package=THT]
  Part2 = Arduino Uno (Rev3) - ICSP
  R4 = Photocell (LDR) [package=THT]
  LED2 = LED - 5mm [color="Red (633nm)" package="5 mm [THT]"]

nets:
  N1: R5.Pin_0, Part2.A1, R4.pin_1
  N2: R5.Pin_1, Part2.GND, LED2.cathode
  N3: R6.Pin_0, LED2.anode
  N4: R6.Pin_1, Part2.D9_PWM
  N5: Part2.5V, R4.pin_0

// code stored in the sketch: cau13-quangtro-1led-sangdan.ino
const int LDR_PIN = A0;
const int LED_PIN = 9;
int lightValue = 0;
int ledBrightness = 0;

void setup() {
  pinMode(LED_PIN, OUTPUT);
  Serial.begin(9600);
}

void loop() {
  lightValue = analogRead(LDR_PIN);
  ledBrightness = map(lightValue, 0, 1023, 0, 255);

  analogWrite(LED_PIN, ledBrightness);

  Serial.print("Giá tr? ánh sáng: ");
  Serial.print(lightValue);
  Serial.print(" -> ?? sáng LED: ");
  Serial.println(ledBrightness);

  delay(500);
}
