# Fritzing sketch cau14-quangtro-coi-keu (saved by Fritzing 0.9.3b)
breadboards: 1

parts:
  Part3 = Arduino Uno (Rev3) - ICSP
  R7 = Photocell (LDR) [package=THT]
  R8 = Resistor [tolerance=±5% resistance=220 package=THT]
  J1 = Piezo Speaker

nets:
  N1: Part3.A1, R7.pin_1, R8.Pin_0
  N2: Part3.D8, J1.pin2
  N3: Part3.5V, R7.pin_0
  N4: Part3.GND, R8.Pin_1, J1.pin1

// code stored in the sketch: cau14-quangtro-coi-keu.ino
const int LDR_PIN = A0;
const int BUZZER_PIN = 8;
int lightValue = 0;

void setup() {
  pinMode(BUZZER_PIN, OUTPUT);
  Serial.begin(9600);
}

void loop() {
  lightValue = analogRead(LDR_PIN);

  Serial.print("Giá tr? ánh sáng: ");
  Serial.print(lightValue);

  if (lightValue < 500) {
    digitalWrite(BUZZER_PIN, HIGH); // Còi kêu
    Serial.println(" -> Còi ?ang kêu");
  } else {
    digitalWrite(BUZZER_PIN, LOW); // Còi t?t
    Serial.println(" -> Còi ?ang t?t");
  }

  delay(500);
}
