# Fritzing sketch cau18-LCD-Nhap-demlui (saved by Fritzing 0.9.3b)
breadboards: 1

parts:
  Part5 = Arduino Uno (Rev3) - ICSP
  R5 = Resistor [tolerance=±5% resistance=220 package=THT]
  U9 = LCD-16X2 [package=lcd-16x2]
  U10 = POT_SWITCH [package=pot_pth_switch]

nets:
  N1: Part5.ICSP_MISO, Part5.D12/MISO, U9.RS
  N2: Part5.D11_PWM/MOSI, U9.E
  N3: Part5.D4, U9.DB4
  N4: Part5.D5_PWM, U9.DB5
  N5: Part5.D6_PWM, U9.DB6
  N6: Part5.D7, U9.DB7
  5V: Part5.5V, R5.Pin_1, U9.VDD, U9.K, U10.G$1_A
  GND: Part5.GND, U9.VSS, U9.R_W, U10.G$2_2
  N7: R5.Pin_0, U9.A
  N8: U9.VO, U10.G$2_1

// code stored in the sketch: cau18-LCD-Nhap-demlui.ino
#include <LiquidCrystal.h>

LiquidCrystal lcd(12, 11, 4, 5, 6, 7);
int n;

void setup() {
  Serial.begin(9600);
  lcd.begin(16, 2);
  lcd.print("Nhap 0..9:");
}

void loop() {
  if (Serial.available()) {
    n = Serial.parseInt();          // ??c s? nguyên
    n = constrain(n, 0, 9);         // Gi?i h?n 0?9
    
    // ??m ng??c
    for (int i = n; i >= 0; i--) {
      lcd.clear();
      lcd.setCursor(0, 0);
      lcd.print("Count down:");
      lcd.setCursor(0, 1);
      lcd.print(i);
      delay(500);
    }
    
    // Sau khi v? 0, yêu c?u nh?p l?i
    lcd.clear();
    lcd.print("Nhap 0..9:");
    // Xóa buffer n?u c?n
    while (Serial.available()) Serial.read();
  }
}
