# Fritzing sketch cau19-LCD-quangtro-1led (saved by Fritzing 0.9.3b)
breadboards: 1

parts:
  Part3 = Arduino Uno (Rev3) - ICSP
  U7 = LCD-16X2 [package=lcd-16x2]
  U8 = POT_SWITCH [package=pot_pth_switch]
  R7 = Resistor [tolerance=±5% resistance=220 package=THT]
  R8 = Resistor [tolerance=±5% resistance=220 package=THT]
  LED3 = LED - 5mm [color="Red (633nm)" package="5 mm [THT]"]
  R9 = Photocell (LDR) [package=THT]
  R10 = Resistor [tolerance=±5% resistance=220 package=THT]

nets:
  N1: Part3.A0, R9.pin_0, R10.Pin_1
  N2: Part3.ICSP_MISO, Part3.D12/MISO, U7.RS
  GND: Part3.GND, U7.VSS, U7.R_W, U8.G$2_2, LED3.cathode, R10.Pin_0
  N3: Part3.D11_PWM/MOSI, U7.E
  N4: Part3.D13/SCK, R8.Pin_1
  N5: Part3.D4, U7.DB4
  N6: Part3.D5_PWM, U7.DB5
  N7: Part3.D6_PWM, U7.DB6
  N8: Part3.D7, U7.DB7
  5V: Part3.5V, U7.VDD, U7.K, U8.G$1_A, R7.Pin_1, R9.pin_1
  N9: U7.VO, U8.G$2_1
  N10: U7.A, R7.Pin_0
  N11: R8.Pin_0, LED3.anode

// code stored in the sketch: cau19-LCD-quangtro-1led.ino
#include <LiquidCrystal.h>

LiquidCrystal lcd(12, 11, 4, 5, 6, 7);
const int sensorPin = A0;
const int ledPin    = 13;

void setup() {
  lcd.begin(16, 2);
  pinMode(ledPin, OUTPUT);
}

void loop() {
  int raw  = analogRead(sensorPin);
  int temp = map(raw, 0, 1023, 0, 100);

  // Hi?n th? LCD
  lcd.clear();
  lcd.setCursor(0, 0);
  lcd.print("Nhiet do:");
  lcd.print(temp);
  lcd.print((char)223);
  lcd.print("C");

  // ?i?u khi?n LED
  if (temp > 30) {
    digitalWrite(ledPin, HIGH);
  } else {
    digitalWrite(ledPin, LOW);
  }

  delay(1000);
}
