# Fritzing sketch cau20-LCD-Nhietdo-1Led (saved by Fritzing 0.9.3b)
breadboards: 1

parts:
  Part1 = Arduino Uno (Rev3) - ICSP
  U1 = LCD-16X2 [package=lcd-16x2]
  U2 = POT_SWITCH [package=pot_pth_switch]
  R1 = Resistor [tolerance=±5% resistance=220 package=THT]
  U3 = POT_SWITCH [package=pot_pth_switch]
  R2 = Resistor [tolerance=±5% resistance=220 package=THT]
  LED1 = LED - 5mm [color="Red (633nm)" package="5 mm [THT]"]

nets:
  N1: Part1.A1, U3.G$2_1
  N2: Part1.ICSP_MISO, Part1.D12/MISO, U1.RS
  N3: Part1.D8, R2.Pin_1
  N4: Part1.D11_PWM/MOSI, U1.E
  N5: Part1.D4, U1.DB4
  N6: Part1.D5_PWM, U1.DB5
  N7: Part1.D6_PWM, U1.DB6
  N8: Part1.D7, U1.DB7
  5V: Part1.5V, U1.VDD, U1.K, U2.G$1_A, R1.Pin_1, U3.G$1_A
  GND: Part1.GND, U1.VSS, U1.R_W, U2.G$2_2, U3.G$2_2, LED1.cathode
  N9: U1.VO, U2.G$2_1
  N10: U1.A, R1.Pin_0
  N11: R2.Pin_0, LED1.anode

// code stored in the sketch: cau20-LCD-Nhietdo-1Led.ino
#include <LiquidCrystal.h>

// Kh?i t?o LCD: RS=12, E=11, D4=4, D5=5, D6=6, D7=7
LiquidCrystal lcd(12, 11, 4, 5, 6, 7);

const int sensorPin = A1;
const int ledPin    = 8;

void setup() {
  lcd.begin(16, 2);
  pinMode(ledPin, OUTPUT);
}

void loop() {
  int raw = analogRead(sensorPin);  
  // Map th?ng raw [0..1023] ? temp [0..100]
  int temp = map(raw, 0, 1023, 0, 100);

  // Hi?n th? lên LCD
  lcd.clear();
  lcd.setCursor(0, 0);
  lcd.print("Nhiet do: ");
  lcd.print(temp);
  lcd.print((char)223); // ký t? ??
  lcd.print("C");

  // ?i?u khi?n LED
  if (temp >= 35) {
    // Nh?p nháy 3 l?n
    for (int i = 0; i < 3; i++) {
      digitalWrite(ledPin, HIGH);
      delay(300);
      digitalWrite(ledPin, LOW);
      delay(300);
    }
  }
  else if (temp >= 30) {
    // Sáng liên t?c
    digitalWrite(ledPin, HIGH);
  }
  else {
    // T?t
    digitalWrite(ledPin, LOW);
  }

  delay(1000); // ??c m?i 1s
}
