# Fritzing sketch cau21-LCD-Nhap-cho-truoc (saved by Fritzing 0.9.3b)
breadboards: 1

parts:
  Part3 = Arduino Uno (Rev3) - ICSP
  U5 = LCD-16X2 [package=lcd-16x2]
  U6 = POT_SWITCH [package=pot_pth_switch]
  R3 = Resistor [tolerance=±5% resistance=220 package=THT]

nets:
  N1: Part3.ICSP_MISO, Part3.D12/MISO, U5.RS
  N2: Part3.D11_PWM/MOSI, U5.E
  N3: Part3.D4, U5.DB4
  N4: Part3.D5_PWM, U5.DB5
  N5: Part3.D6_PWM, U5.DB6
  N6: Part3.D7, U5.DB7
  5V: Part3.5V, U5.VDD, U5.K, U6.G$1_A, R3.Pin_1
  GND: Part3.GND, U5.VSS, U5.R_W, U6.G$2_2
  N7: U5.VO, U6.G$2_1
  N8: U5.A, R3.Pin_0
