# Fritzing sketch cau21-LCD-quangtro-coi-1led (saved by Fritzing 0.9.3b)
breadboards: 1

parts:
  Part2 = Arduino Uno (Rev3) - ICSP
  U5 = LCD-16X2 [package=lcd-16x2]
  U6 = POT_SWITCH [package=pot_pth_switch]
  R3 = Resistor [tolerance=±5% resistance=220 package=THT]
  R4 = Resistor [tolerance=±5% resistance=220 package=THT]
  LED2 = LED - 5mm [color="Red (633nm)" package="5 mm [THT]"]
  R5 = Photocell (LDR) [package=THT]
  J1 = Piezo Speaker
  R6 = Resistor [tolerance=±5% resistance=220 package=THT]

nets:
  N1: Part2.A0, R5.pin_0, R6.Pin_1
  N2: Part2.ICSP_MISO, Part2.D12/MISO, U5.RS
  GND: Part2.GND, U5.VSS, U5.R_W, U6.G$2_2, LED2.cathode, J1.pin1, R6.Pin_0
  N3: Part2.D8, R4.Pin_1
  N4: Part2.D9_PWM, J1.pin2
  N5: Part2.D11_PWM/MOSI, U5.E
  N6: Part2.D4, U5.DB4
  N7: Part2.D5_PWM, U5.DB5
  N8: Part2.D6_PWM, U5.DB6
  N9: Part2.D7, U5.DB7
  5V: Part2.5V, U5.VDD, U5.K, U6.G$1_A, R3.Pin_1, R5.pin_1
  N10: U5.VO, U6.G$2_1
  N11: U5.A, R3.Pin_0
  N12: R4.Pin_0, LED2.anode

// code stored in the sketch: cau21-LCD-quangtro-coi-1led.ino
#include <LiquidCrystal.h>

LiquidCrystal lcd(12, 11, 4, 5, 6, 7);

const int sensorPin = A0;
const int ledPin    = 8;
const int buzzerPin = 9;

void setup() {
  lcd.begin(16, 2);
  pinMode(ledPin, OUTPUT);
  pinMode(buzzerPin, OUTPUT);
}

void loop() {
  int raw = analogRead(sensorPin);
  int temp = map(raw, 0, 1023, 0, 100);

  // Hi?n th? LCD
  lcd.clear();
  lcd.setCursor(0, 0);
  lcd.print("Nhiet do: ");
  lcd.print(temp);
  lcd.print((char)223);
  lcd.print("C");

  // ?i?u ki?n ?i?u khi?n LED & Buzzer
  if (temp > 40) {
    // Buzzer kêu liên t?c, LED t?t
    digitalWrite(ledPin, LOW);
    tone(buzzerPin, 1000); // ng?u ch?n 1?kHz
  }
  else if (temp >= 30) {
    // LED sáng, buzzer t?t
    digitalWrite(ledPin, HIGH);
    noTone(buzzerPin);
  }
  else {
    // D??i 30°C: t?t c?
    digitalWrite(ledPin, LOW);
    noTone(buzzerPin);
  }

  delay(1000);
}
