# Fritzing sketch cau22-LCD-DangNhap (saved by Fritzing 0.9.3b)
breadboards: 1

parts:
  Part2 = Arduino Uno (Rev3) - ICSP
  U3 = LCD-16X2 [package=lcd-16x2]
  U4 = POT_SWITCH [package=pot_pth_switch]
  R2 = Resistor [tolerance=±5% resistance=220 package=THT]

nets:
  N1: Part2.ICSP_MISO, Part2.D12/MISO, U3.RS
  N2: Part2.D11_PWM/MOSI, U3.E
  N3: Part2.D4, U3.DB4
  N4: Part2.D5_PWM, U3.DB5
  N5: Part2.D6_PWM, U3.DB6
  N6: Part2.D7, U3.DB7
  5V: Part2.5V, U3.VDD, U3.K, U4.G$1_A, R2.Pin_1
  GND: Part2.GND, U3.VSS, U3.R_W, U4.G$2_2
  N7: U3.VO, U4.G$2_1
  N8: U3.A, R2.Pin_0

// code stored in the sketch: cau22-LCD-DangNhap.ino
#include <LiquidCrystal.h>

const char* USERNAME = "admin";
const char* PASSWORD = "123";

// Kh?i t?o LCD v?i chân RS=12, E=11, D4=4, D5=5, D6=6, D7=7
LiquidCrystal lcd(12, 11, 4, 5, 6, 7);

void setup() {
  Serial.begin(9600);
  lcd.begin(16, 2);
  lcd.print("Nhap tai khoan:");
  Serial.println("Nhap tai khoan:");
}

void loop() {
  // ??c username
  while (!Serial.available()) {}
  String user = Serial.readStringUntil('\n');
  user.trim();

  if (user != USERNAME) {
    lcd.clear();
    lcd.print("Nhap sai, nhap lai");
    delay(1000);
    lcd.clear();
    lcd.print("Nhap tai khoan:");
    return;
  }

  // ?úng username ? h?i m?t kh?u
  lcd.clear();
  lcd.print("Nhap mat khau:");
  Serial.println("Nhap mat khau:");

  while (!Serial.available()) {}
  String pass = Serial.readStringUntil('\n');
  pass.trim();

  if (pass != PASSWORD) {
    lcd.clear();
    lcd.print("Nhap sai MK");
    delay(1000);
    lcd.clear();
    lcd.print("Nhap tai khoan:");
    return;
  }

  // ??ng nh?p thành công
  lcd.clear();
  lcd.print("Dang nhap TC");
  while (true) {}
}
