# Fritzing sketch cau22-LCD-Nhap-cho-truoc (saved by Fritzing 0.9.3b)
breadboards: 1

parts:
  Part3 = Arduino Uno (Rev3) - ICSP
  U5 = LCD-16X2 [package=lcd-16x2]
  U6 = POT_SWITCH [package=pot_pth_switch]
  R3 = Resistor [tolerance=±5% resistance=220 package=THT]

nets:
  N1: Part3.ICSP_MISO, Part3.D12/MISO, U5.RS
  N2: Part3.D11_PWM/MOSI, U5.E
  N3: Part3.D4, U5.DB4
  N4: Part3.D5_PWM, U5.DB5
  N5: Part3.D6_PWM, U5.DB6
  N6: Part3.D7, U5.DB7
  5V: Part3.5V, U5.VDD, U5.K, U6.G$1_A, R3.Pin_1
  GND: Part3.GND, U5.VSS, U5.R_W, U6.G$2_2
  N7: U5.VO, U6.G$2_1
  N8: U5.A, R3.Pin_0

// code stored in the sketch: cau21-LCD-Nhap-cho-truoc.ino
#include <LiquidCrystal.h>

const char* TARGET = "VIETNAM";

LiquidCrystal lcd(12, 11, 4, 5, 6, 7);

void setup() {
  Serial.begin(9600);
  lcd.begin(16, 2);
  lcd.print("Hay nhap 7 ky tu:");
}

void loop() {
  // ??c xâu
  while (!Serial.available()) {}
  String input = Serial.readStringUntil('\n');
  input.trim();

  lcd.clear();
  if (input == TARGET) {
    lcd.setCursor(0, 0);
    lcd.print("DA NHAP DUNG:");
    lcd.setCursor(0, 1);
    lcd.print(TARGET);
    while (true) {}
  } else {
    lcd.setCursor(0, 0);
    lcd.print(input.substring(0, 16));
    lcd.setCursor(0, 1);
    lcd.print("HAY NHAP LAI");
    delay(1500);
    lcd.clear();
    lcd.print("Hay nhap 7 ky tu:");
  }
}
