# Fritzing sketch cau39-led7-1-nut-tangdan (saved by Fritzing 0.9.3b)
breadboards: 1

parts:
  R1 = Resistor [tolerance=±5% resistance=220 package=THT]
  S1 = Pushbutton [package="[THT]"]
  DI1 = 7-Segment LED Display [package=THT]
  Part1 = Arduino Uno (Rev3) - ICSP
  R2 = Resistor [tolerance=±5% resistance=220 package=THT]

nets:
  N1: R1.Pin_0, S1.Pin_1, S1.Pin_2, Part1.D5_PWM
  N2: R1.Pin_1, Part1.GND, R2.Pin_1
  N3: S1.Pin_3, S1.Pin_4, Part1.5V
  N4: DI1.cathodeE, Part1.D7
  N5: DI1.cathodeD, Part1.D6_PWM
  N6: DI1.commAnode#2, R2.Pin_0
  N7: DI1.cathodeC, Part1.D4
  N8: DI1.cathodeB, Part1.D3_PWM
  N9: DI1.cathodeA, Part1.D2
  N10: DI1.cathodeF, Part1.D8
  N11: DI1.cathodeG, Part1.D9_PWM

// code stored in the sketch: cau39-led7-1-nut-tangdan.ino
int led[] = {2, 3, 4, 9, 6, 8, 7}; // LED 7 ?o?n: A, B, C, D, E, F, G

int mtso[10][7] = {
  {1, 1, 1, 1, 1, 1, 0}, // 0
  {0, 1, 1, 0, 0, 0, 0}, // 1
  {1, 1, 0, 1, 1, 0, 1}, // 2
  {1, 1, 1, 1, 0, 0, 1}, // 3
  {0, 1, 1, 0, 0, 1, 1}, // 4
  {1, 0, 1, 1, 0, 1, 1}, // 5
  {1, 0, 1, 1, 1, 1, 1}, // 6
  {1, 1, 1, 0, 0, 0, 0}, // 7
  {1, 1, 1, 1, 1, 1, 1}, // 8
  {1, 1, 1, 1, 0, 1, 1}  // 9
};

const int nutNhan = 5; 
int so = 0;

void setup() {
  for (int i = 0; i < 7; i++) {
    pinMode(led[i], OUTPUT);
  }

  pinMode(nutNhan, INPUT); 

  HienThiSo(so); 
}

void loop() {
  
  if (digitalRead(nutNhan) == HIGH) {
    delay(50); 
    so++;
    if (so > 9) so = 0;
    HienThiSo(so);

    
    while (digitalRead(nutNhan) == HIGH) {
      delay(10);
    }
  }
}


void HienThiSo(int so) {
  for (int i = 0; i < 7; i++) {
    digitalWrite(led[i], mtso[so][i]);
  }
}
