# Fritzing sketch cau40-ledRGB-3nut (saved by Fritzing 0.9.3b)
breadboards: 1

parts:
  LED1 = RGB LED (com. cathode, rgb) [package="5 mm [THT]"]
  R1 = Resistor [tolerance=±5% resistance=220 package=THT]
  R2 = Resistor [tolerance=±5% resistance=220 package=THT]
  R3 = Resistor [tolerance=±5% resistance=220 package=THT]
  S1 = Pushbutton [package="[THT]"]
  S2 = Pushbutton [package="[THT]"]
  S3 = Pushbutton [package="[THT]"]
  R4 = Resistor [tolerance=±5% resistance=220 package=THT]
  R5 = Resistor [tolerance=±5% resistance=220 package=THT]
  R6 = Resistor [tolerance=±5% resistance=220 package=THT]
  Part1 = Arduino Uno (Rev3) - ICSP

nets:
  N1: LED1.red_anode, R1.Pin_1
  N2: LED1.common_cathode, R4.Pin_1, R5.Pin_1, R6.Pin_1, Part1.GND
  N3: LED1.green_anode, R2.Pin_1
  N4: LED1.blue_anode, R3.Pin_1
  N5: R1.Pin_0, Part1.D7
  N6: R2.Pin_0, Part1.D8
  N7: R3.Pin_0, Part1.D9_PWM
  N8: S1.Pin_1, S1.Pin_2, R4.Pin_0, Part1.D10_PWM/SS
  N9: S1.Pin_3, S1.Pin_4, S2.Pin_3, S2.Pin_4, S3.Pin_3, S3.Pin_4, Part1.5V
  N10: S2.Pin_1, S2.Pin_2, R5.Pin_0, Part1.D11_PWM/MOSI
  N11: S3.Pin_1, S3.Pin_2, R6.Pin_0, Part1.D12/MISO

// code stored in the sketch: cau40-ledRGB-3nut.ino
const int redPin = 7;
const int greenPin = 8;
const int bluePin = 9;

const int buttonR = 10;
const int buttonG = 11;
const int buttonB = 12;

void setup() {
  pinMode(redPin, OUTPUT);
  pinMode(greenPin, OUTPUT);
  pinMode(bluePin, OUTPUT);

  pinMode(buttonR, INPUT_PULLUP);
  pinMode(buttonG, INPUT_PULLUP);
  pinMode(buttonB, INPUT_PULLUP);
}

void loop() {
  digitalWrite(redPin, digitalRead(buttonR) == LOW ? HIGH : LOW);
  digitalWrite(greenPin, digitalRead(buttonG) == LOW ? HIGH : LOW);
  digitalWrite(bluePin, digitalRead(buttonB) == LOW ? HIGH : LOW);
}
