# Fritzing sketch cau41-3led-random (saved by Fritzing 0.9.3b)
breadboards: 1

parts:
  R1 = Resistor [tolerance=±5% resistance=220 package=THT]
  R2 = Resistor [tolerance=±5% resistance=220 package=THT]
  R3 = Resistor [tolerance=±5% resistance=220 package=THT]
  LED1 = LED - 5mm [color="Red (633nm)" package="5 mm [THT]"]
  LED2 = LED - 5mm [color="Red (633nm)" package="5 mm [THT]"]
  LED3 = LED - 5mm [color="Red (633nm)" package="5 mm [THT]"]
  Part1 = Arduino Uno (Rev3) - ICSP

nets:
  N1: R1.Pin_0, LED1.anode
  N2: R1.Pin_1, Part1.D3_PWM
  N3: R2.Pin_0, LED2.anode
  N4: R2.Pin_1, Part1.D4
  N5: R3.Pin_0, LED3.anode
  N6: R3.Pin_1, Part1.D5_PWM
  N7: LED1.cathode, LED2.cathode, LED3.cathode, Part1.GND

// code stored in the sketch: cau41-3led-random.ino
int leds[] = {3, 4, 5};

void setup() {
  for (int i = 0; i < 3; i++) {
    pinMode(leds[i], OUTPUT);
    digitalWrite(leds[i], LOW); // Kh?i t?o t?t
  }

  randomSeed(analogRead(0)); // T?o s? ng?u nhiên
}

void loop() {
  int a = random(1, 4); // 1 ??n 3

  for (int i = 0; i < 3; i++) {
    digitalWrite(leds[i], (a == i + 1) ? HIGH : LOW);
  }

  delay(1000);
}
