# Fritzing sketch cau45-3led-3nut (saved by Fritzing 0.9.3b)
breadboards: 1

parts:
  Part1 = Arduino Uno (Rev3) - ICSP
  S1 = Pushbutton [package="[THT]"]  # not connected
  R1 = Resistor [tolerance=±5% resistance=220 package=THT]
  LED1 = LED - 5mm [color="Red (633nm)" package="5 mm [THT]"]
  R2 = Resistor [tolerance=±5% resistance=220 package=THT]
  LED2 = LED - 5mm [color="Red (633nm)" package="5 mm [THT]"]
  S2 = Pushbutton [package="[THT]"]
  R3 = Resistor [tolerance=±5% resistance=220 package=THT]
  R4 = Resistor [tolerance=±5% resistance=220 package=THT]
  LED3 = LED - 5mm [color="Red (633nm)" package="5 mm [THT]"]
  S3 = Pushbutton [package="[THT]"]
  R5 = Resistor [tolerance=±5% resistance=220 package=THT]
  R6 = Resistor [tolerance=±5% resistance=220 package=THT]

nets:
  N1: Part1.ICSP_MISO, Part1.D12/MISO, S3.Pin_1, S3.Pin_2, R5.Pin_0
  N2: Part1.D8, R4.Pin_1
  N3: Part1.D10_PWM/SS, R1.Pin_0
  N4: Part1.D11_PWM/MOSI, S2.Pin_1, S2.Pin_2, R3.Pin_0
  N5: Part1.D7, R2.Pin_1
  N6: Part1.5V, S2.Pin_3, S2.Pin_4, S3.Pin_3, S3.Pin_4
  N7: Part1.GND, R1.Pin_1, LED1.cathode, LED2.cathode, R3.Pin_1, LED3.cathode, R5.Pin_1
  N8: LED1.anode, R2.Pin_0
  N9: LED2.anode, R4.Pin_0
  N10: LED3.anode, R6.Pin_0

// code stored in the sketch: cau45-3led-3nut.ino
int leds[] = {7, 8, 9};
int buttons[] = {10, 11, 12};

void setup() {
  for (int i = 0; i < 3; i++) {
    pinMode(leds[i], OUTPUT);
    pinMode(buttons[i], INPUT);
  }
}

void loop() {
  for (int i = 0; i < 3; i++) {
    if (digitalRead(buttons[i]) == HIGH) {
      digitalWrite(leds[i], HIGH);
    } else {
      digitalWrite(leds[i], LOW);
    }
  }
}
