# Fritzing sketch cau46-led7-2led-tong (saved by Fritzing 0.9.3b)
breadboards: 1

parts:
  Part2 = Arduino Uno (Rev3) - ICSP
  DI2 = 7-Segment LED Display [package=THT]
  R4 = Resistor [tolerance=±5% resistance=220 package="2512 [SMD]"]
  LED1 = LED - 5mm [color="Red (633nm)" package="5 mm [THT]"]
  LED2 = LED - 5mm [color="Red (633nm)" package="5 mm [THT]"]
  R5 = Resistor [tolerance=±5% resistance=220 package=THT]
  R6 = Resistor [tolerance=±5% resistance=220 package=THT]

nets:
  N1: Part2.D8, DI2.cathodeE
  N2: Part2.D9_PWM, DI2.cathodeF
  N3: Part2.D10_PWM/SS, DI2.cathodeG
  N4: Part2.D2, DI2.cathodeA
  N5: Part2.D3_PWM, DI2.cathodeB
  N6: Part2.D4, DI2.cathodeC
  N7: Part2.D5_PWM, R6.Pin_1
  N8: Part2.D6_PWM, R5.Pin_1
  N9: Part2.D7, DI2.cathodeD
  N10: Part2.GND, R4.Pin_1, LED1.cathode, LED2.cathode
  N11: DI2.commAnode#2, R4.Pin_0
  N12: LED1.anode, R6.Pin_0
  N13: LED2.anode, R5.Pin_0

// code stored in the sketch: cau46-led7-2led-tong.ino
int led[] = {2, 3, 4, 7, 8, 9, 10}; // LED 7 ?o?n: A, B, C, D, E, F, G
int L1 = 5;
int L2 = 6;

int mtso[11][7] = {
  {1, 1, 1, 1, 1, 1, 0}, // 0
  {0, 1, 1, 0, 0, 0, 0}, // 1
  {1, 1, 0, 1, 1, 0, 1}, // 2
  {1, 1, 1, 1, 0, 0, 1}, // 3
  {0, 1, 1, 0, 0, 1, 1}, // 4
  {1, 0, 1, 1, 0, 1, 1}, // 5
  {1, 0, 1, 1, 1, 1, 1}, // 6
  {1, 1, 1, 0, 0, 0, 0}, // 7
  {1, 1, 1, 1, 1, 1, 1}, // 8
  {1, 1, 1, 1, 0, 1, 1}, // 9
};

void setup() {
  for (int i = 0; i < 7; i++) {
    pinMode(led[i], OUTPUT);
  }
  pinMode(L1, OUTPUT);
  pinMode(L2, OUTPUT);

  randomSeed(analogRead(0)); 
}

void loop() {
  int a = random(0, 6); 
  int b = random(0, 6);
  int tong = a + b;

  HienThiSo(tong);

  if (a > 3) {
    digitalWrite(L1, HIGH);
    digitalWrite(L2, LOW);
  } else {
    digitalWrite(L1, LOW);
    digitalWrite(L2, HIGH);
  }

  delay(3000); 
}


void HienThiSo(int so) {
  for (int i = 0; i < 7; i++) {
    digitalWrite(led[i], mtso[so][i]);
  }
}
