# Fritzing sketch cau6_ledXanhDo_bientro (saved by Fritzing 0.9.3b)
breadboards: 1

parts:
  Part1 = Arduino Uno (Rev3) - ICSP
  LED1 = smd LED [color="Green (555nm)" package="1206 [SMD]"]
  LED2 = smd LED [color="Red (633nm)" package="1206 [SMD]"]
  R1 = Resistor [tolerance=±5% resistance=220 package="2010 [SMD]"]
  R2 = Resistor [tolerance=±5% resistance=220 package="2010 [SMD]"]
  U1 = POT_SWITCH [package=pot_pth_switch]

nets:
  N1: Part1.A0, U1.G$2_1
  N2: Part1.D8, R1.Pin_1
  N3: Part1.D9_PWM, R2.Pin_1
  N4: Part1.GND, LED1.cathode, LED2.cathode, U1.G$1_A, U1.G$2_2
  N5: LED1.anode, R1.Pin_0
  N6: LED2.anode, R2.Pin_0

// code stored in the sketch: Bai6_ledXanhDo_Bientro.ino
// Khai báo chân
const int potPin = A0;      // Chân analog ??c bi?n tr?
const int ledGreen = 8;     // LED xanh
const int ledRed = 9;       // LED ??

void setup() {
  Serial.begin(9600);       // Kh?i ??ng Serial Monitor
  pinMode(ledGreen, OUTPUT);
  pinMode(ledRed, OUTPUT);
}

void loop() {
  int sensorValue = analogRead(potPin);  // ??c giá tr? analog (0-1023)
  
  // Chuy?n ??i giá tr? analog thành nhi?t ?? (0-100°C)
  int temperature = map(sensorValue, 0, 1023, 0, 100);

  // Hi?n th? nhi?t ??
  Serial.print("Nhiet do: ");
  Serial.print(temperature);
  Serial.print(" °C - ");

  // ?i?u khi?n LED
  if (temperature < 30) {
    digitalWrite(ledGreen, HIGH);
    digitalWrite(ledRed, LOW);
    Serial.println("LED xanh dang sang");
  }
  else if (temperature > 70) {
    digitalWrite(ledGreen, LOW);
    digitalWrite(ledRed, HIGH);
    Serial.println("LED do dang sang");
  }
  else {
    digitalWrite(ledGreen, LOW);
    digitalWrite(ledRed, LOW);
    Serial.println("Khong co LED nao sang");
  }

  delay(500);  // ??c l?i sau 0.5 giây
}
