# Fritzing sketch cau7_ledXanhDo(3NhietDo)_Bientro (saved by Fritzing 0.9.3b)
breadboards: 1

parts:
  Part2 = Arduino Uno (Rev3) - ICSP
  LED4 = smd LED [color="Red (633nm)" package="1206 [SMD]"]
  R3 = Resistor [tolerance=±5% resistance=220 package="2010 [SMD]"]
  R4 = Resistor [tolerance=±5% resistance=220 package="2010 [SMD]"]
  U2 = POT_SWITCH [package=pot_pth_switch]
  LED5 = LED - 5mm [color="Green (555nm)" package="5 mm [THT]"]

nets:
  N1: Part2.A0, U2.G$2_1
  N2: Part2.D8, R3.Pin_1
  N3: Part2.D9_PWM, R4.Pin_1
  N4: Part2.GND, LED4.cathode, U2.G$1_A, U2.G$2_2, LED5.cathode
  N5: LED4.anode, R4.Pin_0
  N6: R3.Pin_0, LED5.anode

// code stored in the sketch: Bai7_ledXanhDo(3NhietDo)_bientro.ino
// Khai báo chân
const int potPin = A0;       // Chân analog ??c bi?n tr?
const int led1 = 8;          // LED 1
const int led2 = 9;          // LED 2

void setup() {
  Serial.begin(9600);        // B?t ??u giao ti?p Serial
  pinMode(led1, OUTPUT);
  pinMode(led2, OUTPUT);
}

void loop() {
  int sensorValue = analogRead(potPin);    // ??c giá tr? t? bi?n tr?
  int temperature = map(sensorValue, 0, 1023, 0, 100);   // Chuy?n ??i thành nhi?t ??

  // In ra Serial Monitor
  Serial.print("Nhiet do: ");
  Serial.print(temperature);
  Serial.print(" °C - ");

  // X? lý  t?t ?èn theo nhi?t ??
  if (temperature <= 30) {
    digitalWrite(led1, LOW);
    digitalWrite(led2,LOW);
    Serial.println("Ca 2 den tat sang");
  } 
  else if (temperature > 30 && temperature <= 50) {
    digitalWrite(led1, HIGH);
    digitalWrite(led2, LOW);
    Serial.println("Chi den 1 sang");
  } 
  else if (temperature > 50 && temperature <= 80) {
    digitalWrite(led1, LOW);
    digitalWrite(led2, HIGH);
    Serial.println("Chi den 2 sang");
  } 
  else { // temperature > 80
    digitalWrite(led1, HIGH);
    digitalWrite(led2, HIGH);
    Serial.println("Ca 2 den dang sang");
  }

  delay(500);  // ??i 0.5 giây tr??c l?n ??c ti?p theo
}
