# Fritzing sketch cau8_1Led(SangDan)_Bientro (saved by Fritzing 0.9.3b)
breadboards: 1

parts:
  Part2 = Arduino Uno (Rev3) - ICSP
  LED3 = smd LED [color="Red (633nm)" package="1206 [SMD]"]
  R3 = Resistor [tolerance=±5% resistance=220 package="2010 [SMD]"]
  U2 = POT_SWITCH [package=pot_pth_switch]

nets:
  N1: Part2.A0, U2.G$2_1
  N2: Part2.GND, LED3.cathode, U2.G$1_A, U2.G$2_2
  N3: Part2.D9_PWM, R3.Pin_1
  N4: LED3.anode, R3.Pin_0

// code stored in the sketch: Bai8_1led(SangDan)_Bientro.ino
const int potPin = A0;    // Bi?n tr? ? A0
const int ledPin = 9;     // LED n?i chân PWM D9

void setup() {
  Serial.begin(9600);
  pinMode(ledPin, OUTPUT);
}

void loop() {
  int potValue = analogRead(potPin);               // ??c giá tr? bi?n tr? (0-1023)
  int brightness = map(potValue, 0, 1023, 0, 255);  // Chuy?n thành ?? sáng (0-255)

  analogWrite(ledPin, brightness);                  // ?i?u khi?n ?? sáng LED

  Serial.print("Gia tri bien tro: ");
  Serial.print(potValue);
  Serial.print(" - Do sang LED: ");
  Serial.println(brightness);

  delay(300);
}
