# Fritzing sketch cau9_Coi(TangDan)_Bientro (saved by Fritzing 0.9.3b)
breadboards: 1

parts:
  Part1 = Arduino Uno (Rev3) - ICSP
  J1 = Piezo Speaker
  U3 = POT_SWITCH [package=pot_pth_switch]

nets:
  N1: Part1.A0, U3.G$2_1
  N2: Part1.D10_PWM/SS, J1.pin2
  N3: Part1.5V, U3.G$1_A
  N4: Part1.GND, U3.G$2_2
  N5: Part1.VIN, J1.pin1

// code stored in the sketch: Bai9_Coi(TangDan)_Bientro.ino
const int potPin = A1;    // Bi?n tr? ? A1
const int buzzerPin = 10; // Còi n?i chân PWM D10

void setup() {
  Serial.begin(9600);
  pinMode(buzzerPin, OUTPUT);
}

void loop() {
  int potValue = analogRead(potPin);                // ??c giá tr? bi?n tr? (0-1023)
  int buzzerVolume = map(potValue, 0, 1023, 0, 255); // Chuy?n thành âm l??ng (0-255)

  analogWrite(buzzerPin, buzzerVolume);             // ?i?u ch?nh ?? l?n còi

  Serial.print("Gia tri dien ap (A1): ");
  Serial.print(potValue);
  Serial.print(" - Am luong coi: ");
  Serial.println(buzzerVolume);

  delay(300);
}
